// Logisim project 4_bit_Subtractor.circ as structural Verilog: 2 circuits, main circuit main
module main (
  input  A,
  input  B,
  input  Borrow_in,
  output Diffrense,
  output Borrow_Out
);

  wire and_1_out, and_2_out, not_1_out, not_2_out, xor_1_out;

  xor xor_1 (xor_1_out, A, B);
  not not_1 (not_1_out, xor_1_out);
  not not_2 (not_2_out, A);
  and and_1 (and_1_out, not_1_out, Borrow_in);
  and and_2 (and_2_out, not_2_out, B);
  xor xor_2 (Diffrense, xor_1_out, Borrow_in);
  or or_1 (Borrow_Out, and_1_out, and_2_out);
endmodule

module _4_Bit_Subtractor (
  input  X0,
  input  Y0,
  input  X1,
  input  Y1,
  input  X2,
  input  Y2,
  input  X3,
  input  Y3,
  input  Borrow_In,
  output Borrow_Out,
  output D0,
  output out_12,
  output out_13,
  output out_14
);

  wire main_1_borrow_out, main_2_borrow_out, main_3_borrow_out;

  main main_1 (.A(X0), .B(Y0), .Borrow_in(Borrow_In), .Diffrense(D0), .Borrow_Out(main_1_borrow_out));
  main main_2 (.A(X1), .B(Y1), .Borrow_in(main_1_borrow_out), .Diffrense(out_12), .Borrow_Out(main_2_borrow_out));
  main main_3 (.A(X2), .B(Y2), .Borrow_in(main_2_borrow_out), .Diffrense(out_13), .Borrow_Out(main_3_borrow_out));
  main main_4 (.A(X3), .B(Y3), .Borrow_in(main_3_borrow_out), .Diffrense(out_14), .Borrow_Out(Borrow_Out));

  // Notes on the sheet:
  //   D1
  //   D2
  //   D3
endmodule
