// Logisim project Converting _Half_Adder_to_Full_Adder.circ as structural Verilog: 1 circuit, main circuit main
module main (
  input  X,
  input  Y,
  input  Carry_in,
  output Sum,
  output Carry_out
);

  wire and_1_out, and_2_out, xor_1_out;

  xor xor_1 (xor_1_out, X, Y);
  and and_1 (and_1_out, X, Y);
  and and_2 (and_2_out, xor_1_out, Carry_in);
  xor xor_2 (Sum, xor_1_out, Carry_in);
  or or_1 (Carry_out, and_2_out, and_1_out);
endmodule
