// Logisim project Full_Adder.circ as structural Verilog: 1 circuit, main circuit main
module main (
  input  A,
  input  B,
  input  Carra_in,
  output Sum,
  output carrt_out
);

  wire and_1_out, and_2_out, and_3_out, xor_1_out;

  xor xor_1 (xor_1_out, A, B);
  and and_1 (and_1_out, A, B);
  and and_2 (and_2_out, A, Carra_in);
  and and_3 (and_3_out, B, Carra_in);
  xor xor_2 (Sum, xor_1_out, Carra_in);
  or or_1 (carrt_out, and_1_out, and_2_out, and_3_out);
endmodule
