// Logisim project Full_Subtractor.circ as structural Verilog: 1 circuit, main circuit main
module main (
  input  A,
  input  B,
  input  Borrow_in,
  output Diffrense,
  output Borrow_Out
);

  wire and_1_out, and_2_out, not_1_out, not_2_out, xor_1_out;

  xor xor_1 (xor_1_out, A, B);
  not not_1 (not_1_out, xor_1_out);
  not not_2 (not_2_out, A);
  and and_1 (and_1_out, not_1_out, Borrow_in);
  and and_2 (and_2_out, not_2_out, B);
  xor xor_2 (Diffrense, xor_1_out, Borrow_in);
  or or_1 (Borrow_Out, and_1_out, and_2_out);
endmodule
