// Logisim project Garst.circ as structural Verilog: 1 circuit, main circuit main
module main (
  input  in_1,
  input  in_2,
  input  in_3,
  input  in_4,
  input  in_5,
  input  in_6,
  input  in_7,
  input  in_8,
  input  in_9,
  input  in_10,
  input  in_11,
  input  in_12,
  input  in_13,
  input  in_14,
  input  in_15,
  input  in_16,
  input  in_17,
  input  in_18,
  input  in_19,
  input  in_20,
  input  in_21,
  output out_22,
  output out_23,
  output out_24,
  output out_25,
  output out_26,
  output out_27,
  output out_28,
  output out_29,
  output out_30,
  output out_31,
  output out_32,
  output out_33,
  output out_34
);

  wire nand_1_out, nand_4_out, nand_5_out, nand_6_out, nand_8_out, nand_9_out, nand_12_out, nand_13_out,
       nand_14_out, nand_15_out, nor_1_out, nor_2_out, nor_6_out, nor_7_out, nor_8_out, nor_9_out,
       nor_11_out, nor_13_out, nor_14_out, nor_15_out, not_1_out, not_2_out, not_4_out, not_5_out;

  not not_1 (not_1_out, in_7);
  not not_2 (not_2_out, in_9);
  nand nand_1 (nand_1_out, in_3, in_5);
  nor nor_1 (nor_1_out, in_11, in_11);
  nor nor_2 (nor_2_out, in_13, in_13);
  not not_3 (out_22, in_1);
  nand nand_2 (out_23, in_1, in_1);
  nor nor_3 (out_24, in_1, in_1);
  nor nor_4 (out_28, not_1_out, not_2_out);
  nand nand_3 (out_26, nand_1_out, nand_1_out);
  nor nor_5 (out_30, nor_1_out, nor_2_out);
  nand nand_4 (nand_4_out, in_14, in_16);
  nor nor_6 (nor_6_out, in_18, in_20);
  nand nand_5 (nand_5_out, in_14, nand_4_out);
  nand nand_6 (nand_6_out, nand_4_out, in_16);
  nor nor_7 (nor_7_out, in_18, nor_6_out);
  nor nor_8 (nor_8_out, nor_6_out, in_20);
  nand nand_7 (out_31, nand_5_out, nand_6_out);
  nor nor_9 (nor_9_out, nor_7_out, nor_8_out);
  nor nor_10 (out_33, nor_9_out, nor_9_out);
  nand nand_8 (nand_8_out, in_10, in_10);
  nand nand_9 (nand_9_out, in_12, in_12);
  nor nor_11 (nor_11_out, in_2, in_4);
  not not_4 (not_4_out, in_6);
  not not_5 (not_5_out, in_8);
  nand nand_10 (out_27, not_4_out, not_5_out);
  nor nor_12 (out_25, nor_11_out, nor_11_out);
  nand nand_11 (out_29, nand_8_out, nand_9_out);
  nand nand_12 (nand_12_out, in_15, in_17);
  nor nor_13 (nor_13_out, in_19, in_21);
  nand nand_13 (nand_13_out, in_15, nand_12_out);
  nand nand_14 (nand_14_out, nand_12_out, in_17);
  nor nor_14 (nor_14_out, in_19, nor_13_out);
  nor nor_15 (nor_15_out, nor_13_out, in_21);
  nand nand_15 (nand_15_out, nand_13_out, nand_14_out);
  nor nor_16 (out_34, nor_14_out, nor_15_out);
  nand nand_16 (out_32, nand_15_out, nand_15_out);

  // Notes on the sheet:
  //   AND Gate
  //   AND Gate
  //   NOT Gate
  //   NOT Gate
  //   XOR Gate
  //   Or Gate
  //   XNOR Gate
endmodule
