// Logisim project Half_Adder.circ as structural Verilog: 1 circuit, main circuit main
module main (
  input  X,
  input  Y,
  input  X_2,
  input  Y_2,
  output sum,
  output Carry,
  output sum_2,
  output Carry_2
);

  wire and_2_out, and_3_out, not_1_out, not_2_out;

  not not_1 (not_1_out, Y_2);
  not not_2 (not_2_out, X_2);
  xor xor_1 (sum, X, Y);
  and and_1 (Carry, X, Y);
  and and_2 (and_2_out, X_2, not_1_out);
  and and_3 (and_3_out, Y_2, not_2_out);
  and and_4 (Carry_2, X_2, Y_2);
  or or_1 (sum_2, and_2_out, and_3_out);
endmodule
