// Logisim project Halfl_Subtractor.circ as structural Verilog: 1 circuit, main circuit main
module main (
  input  A,
  input  B,
  output Diffrense,
  output Borrow_Out
);

  wire not_1_out;

  xor xor_1 (Diffrense, A, B);
  not not_1 (not_1_out, A);
  and and_1 (Borrow_Out, not_1_out, B);
endmodule
