// Logisim project JK.circ as structural Verilog: 2 circuits, main circuit main
module main (
  input  in_1,
  input  in_2,
  output out_3,
  output out_4
);

  wire clock_1_out, nand_1_out, nand_2_out;

  Clock clock_1 (.out(clock_1_out));
  nand nand_1 (nand_1_out, out_3, in_1, clock_1_out);
  nand nand_2 (nand_2_out, clock_1_out, in_2, out_4);
  nand nand_3 (out_3, nand_1_out, out_4);
  nand nand_4 (out_4, out_3, nand_2_out);
endmodule

module JK_Filp_Flop (
  input  in_1,
  input  in_2,
  output out_3,
  output out_4
);

  wire clock_1_out, nand_1_out, nand_2_out, nand_3_out, nand_4_out, nand_5_out, nand_6_out;

  Clock clock_1 (.out(clock_1_out));
  nand nand_1 (nand_1_out, in_1, clock_1_out);
  nand nand_2 (nand_2_out, clock_1_out, in_2);
  nand nand_3 (nand_3_out, nand_1_out, nand_4_out);
  nand nand_4 (nand_4_out, nand_3_out, nand_2_out);
  nand nand_5 (nand_5_out, nand_3_out, clock_1_out);
  nand nand_6 (nand_6_out, clock_1_out, nand_4_out);
  nand nand_7 (out_3, nand_5_out, out_4);
  nand nand_8 (out_4, out_3, nand_6_out);
endmodule
