// Logisim project Ripple_carry_adder.circ as structural Verilog: 2 circuits, main circuit main
module main (
  input  in_1,
  input  in_2,
  input  in_3,
  output out_4,
  output out_5
);

  wire and_1_out, and_2_out, and_3_out, xor_1_out;

  xor xor_1 (xor_1_out, in_1, in_2);
  xor xor_2 (out_5, in_3, xor_1_out);
  and and_1 (and_1_out, in_1, in_2);
  and and_2 (and_2_out, in_1, in_3);
  and and_3 (and_3_out, in_2, in_3);
  or or_1 (out_4, and_1_out, and_2_out, and_3_out);
endmodule

module Ripple_carry_adder (
  input  X0,
  input  Y0,
  input  X1,
  input  Y1,
  input  X2,
  input  Y2,
  input  X3,
  input  Y3,
  input  Cin,
  output Cout,
  output out_11,
  output out_12,
  output out_13,
  output out_14
);

  wire main_1_out_4, main_2_out_4, main_3_out_4;

  main main_1 (.in_3(Cin), .out_4(main_1_out_4), .in_1(X0), .in_2(Y0), .out_5(out_11));
  main main_2 (.in_3(main_1_out_4), .out_4(main_2_out_4), .in_1(X1), .in_2(Y1), .out_5(out_12));
  main main_3 (.in_3(main_2_out_4), .out_4(main_3_out_4), .in_1(X2), .in_2(Y2), .out_5(out_13));
  main main_4 (.in_3(main_3_out_4), .out_4(Cout), .in_1(X3), .in_2(Y3), .out_5(out_14));

  // Notes on the sheet:
  //   H/A0
  //   S0
  //   H/A1
  //   S1
  //   H/A2
  //   S2
  //   H/A3
  //   S4
endmodule
