// Logisim project odd_Parity.circ as structural Verilog: 1 circuit, main circuit main
module main (
  input  A,
  input  B,
  input  C,
  input  D,
  output Parite_outut
);

  wire xor_1_out, xor_2_out;

  xor xor_1 (xor_1_out, A, B);
  xor xor_2 (xor_2_out, C, D);
  xor xor_3 (Parite_outut, xor_1_out, xor_2_out);
endmodule
